// Digital circuit MUX.dig as structural Verilog
module MUX (
  input  D,
  input  C,
  input  B,
  input  A,
  output Y
);

  wire and_1_out, and_2_out, not_2_out, not_3_out;
  wire [2:0] undriven;

  // Not not_1 is placed but not wired
  not not_2 (not_2_out, A);
  and and_1 (and_1_out, not_3_out, A);
  not not_3 (not_3_out, D);
  and and_2 (and_2_out, D, not_2_out);
  Multiplexer #(.Selector_Bits(3)) multiplexer_1 (
    .sel(undriven), .in_0(and_2_out), .in_1(and_2_out), .in_2(and_2_out), .in_3(and_2_out), .in_4(and_1_out),
    .in_5(and_1_out), .in_6(and_1_out), .in_7(1'b0), .out(Y));

  // Notes on the sheet:
  //   Use A as the most-significant bit and 
  //   D as the least-significant bit.
  //   Converts between single bits & a 3-bit bus
endmodule

/* Test case:
A B C D Y
0 0 0 0 X
0 0 0 1 1
*/
